// Digital circuit CPU.dig as structural Verilog
module CPU (
  input  CLK,
  input  RegF_WE,
  input  [7:0] in_8bits,
  input  in_20,
  input  in_21,
  input  in_22,
  input  in_23,
  output [7:0] out_8bits,
  output [7:0] ddd,
  output [7:0] sddd,
  output [7:0] out_7,
  output [7:0] out_8,
  output [7:0] out_9,
  output [2:0] out_10,
  output [2:0] out_11,
  output [7:0] out_12,
  output [7:0] out_13,
  output [7:0] out_14,
  output [7:0] out_15,
  output [7:0] out_16,
  output [7:0] out_17,
  output [7:0] out_18,
  output [7:0] out_19
);

  wire and_1_out, and_3_out, Branching_SetUp_q, CLK_t, comparator_1_eq, counter_1_ovf, counterpreset_1_ovf,
       EX_GPIO_en, EX_Jump_do, EX_Jump_en, EX_Math_en, EX_Mem_doLD, EX_Mem_doSTR, EX_Mem_en, Go_Branch,
       ID_IMM_check, ME_do_input, ME_do_output, ME_GPIO___Math, ME_Mem_doMOV, multiplexer_2_out, not_1_out,
       not_2_out, not_3_out, not_4_out, NotNOPing, or_2_out, or_3_out, WB_EN;
  wire [1:0] EX_Do_SMTH;
  wire [2:0] EX_R_Dest, EX_SMTH_Choice, ID_R_Dest, ID_R_Src1, ME_R_Src2, multiplexer_3_out,
       multiplexer_5_out, multiplexer_6_out, register_1_q;
  wire [3:0] ALU_c_f, EX_Reg_F, ID_Opcode;
  wire [4:0] rom_1_d;
  wire [7:0] EX_Data_A, EX_Data_B, EX_Mem_output, ID_R_Src2_IMM, ME_output, ME_output_mov, multiplexer_1_out,
       multiplexer_4_out, multiplexer_11_out, R_Src_2_Out, register_3_q;
  wire [10:0] multiplexer_8_out;
  wire [11:11] ME_WB_q;
  wire [18:0] Instruction_d;
  wire [24:0] EX_ME_out, multiplexer_12_out;

  or or_1 (CLK_t, CLK, in_22, in_21, in_20);
  CounterPreset #(.Bits(8)) counterpreset_1 (
    .en(NotNOPing), .C(CLK_t), .dir(1'b0), .in(EX_Data_B), .ld(Go_Branch), .clr(counterpreset_1_ovf),
    .out(ddd), .ovf(counterpreset_1_ovf));
  or or_2 (or_2_out, Go_Branch, counter_1_ovf);
  Demultiplexer #(.Selector_Bits(2)) demultiplexer_1 (
    .sel(EX_ME_out[20:19]), .in(EX_ME_out[24]), .out_0(ME_do_output), .out_1(ME_do_input),
    .out_2(ME_Mem_doMOV));  // open: out_3
  Multiplexer #(.Bits(8)) multiplexer_1 (
    .sel(ME_do_input), .in_0(R_Src_2_Out), .in_1(in_8bits), .out(multiplexer_1_out));
  or or_3 (or_3_out, multiplexer_2_out, Go_Branch);
  Register Branching_SetUp (.D(or_3_out), .C(CLK_t), .en(or_2_out), .Q(Branching_SetUp_q));
  and and_1 (and_1_out, CLK_t, EX_Mem_en);
  Register #(.Bits(3)) register_1 (.D(EX_ME_out[18:16]), .C(CLK_t), .en(EX_ME_out[24]), .Q(register_1_q));
  Register #(.Bits(8)) register_2 (.D(EX_ME_out[7:0]), .C(CLK_t), .en(ME_Mem_doMOV), .Q(ME_output_mov));
  nand nand_1 (NotNOPing, or_3_out, not_1_out);
  Demultiplexer #(.Selector_Bits(2)) demultiplexer_2 (
    .sel(EX_Do_SMTH), .in(1'b1), .out_0(EX_Math_en), .out_1(EX_GPIO_en), .out_2(EX_Jump_en), .out_3(EX_Mem_en));
  RAMDualPort #(.AddrBits(8), .Bits(8)) ramdualport_1 (
    .A(EX_Data_A), .Din(EX_Data_B), .str(EX_Mem_doSTR), .C(and_1_out), .ld(EX_Mem_doLD), .D(EX_Mem_output));
  Demultiplexer #(.Bits(3)) demultiplexer_3 (.sel(ME_do_output), .in(register_1_q), .out_0(out_10), .out_1(ME_R_Src2));
  Register #(.Bits(8)) register_3 (.D(multiplexer_1_out), .C(CLK_t), .en(EX_ME_out[24]), .Q(register_3_q));
  Demultiplexer demultiplexer_4 (.sel(EX_SMTH_Choice[0]), .in(1'b1), .out_0(EX_Mem_doLD), .out_1(EX_Mem_doSTR));
  Demultiplexer #(.Bits(8)) demultiplexer_5 (
    .sel(ME_do_input), .in(register_3_q), .out_0(out_8bits), .out_1(ME_output));
  ROM #(.AddrBits(8), .Bits(19)) Instruction (.A(ddd), .sel(NotNOPing), .D(Instruction_d));
  Multiplexer multiplexer_2 (.sel(counter_1_ovf), .in_0(Branching_SetUp_q), .in_1(1'b0), .out(multiplexer_2_out));
  Counter counter_1 (.en(Branching_SetUp_q), .C(CLK_t), .clr(counter_1_ovf), .ovf(counter_1_ovf));  // open: out
  or or_4 (ME_GPIO___Math, EX_Math_en, EX_GPIO_en);
  not not_1 (not_1_out, counter_1_ovf);
  not not_2 (not_2_out, in_23);
  // And and_2 has open pins: In_1=CLK_t, In_2=not_2_out, out=open
  Register #(.Bits(19)) IF_ID (
    .D(Instruction_d), .C(CLK_t), .en(1'b1),
    .Q({ID_IMM_check, ID_Opcode, ID_R_Dest, ID_R_Src1, ID_R_Src2_IMM}));
  Multiplexer #(.Bits(3)) multiplexer_3 (.sel(EX_ME_out[24]), .in_0(ID_R_Dest), .in_1(out_10), .out(multiplexer_3_out));
  and and_3 (and_3_out, RegF_WE, NotNOPing);
  Multiplexer #(.Bits(8)) multiplexer_4 (
    .sel(ME_Mem_doMOV), .in_0(ME_output), .in_1(ME_output_mov), .out(multiplexer_4_out));
  Multiplexer #(.Bits(3)) multiplexer_5 (.sel(WB_EN), .in_0(multiplexer_3_out), .in_1(out_11), .out(multiplexer_5_out));
  Multiplexer #(.Bits(3)) multiplexer_6 (
    .sel(EX_ME_out[24]), .in_0(ID_R_Src2_IMM[2:0]), .in_1(ME_R_Src2), .out(multiplexer_6_out));
  ROM #(.AddrBits(4), .Bits(5)) rom_1 (.A(ID_Opcode), .sel(1'b1), .D(rom_1_d));
  Multiplexer #(.Bits(8)) multiplexer_7 (.sel(ID_IMM_check), .in_0(R_Src_2_Out), .in_1(ID_R_Src2_IMM), .out(out_8));
  not not_3 (not_3_out, EX_Reg_F[3]);
  Multiplexer #(.Bits(11)) multiplexer_8 (
    .sel(not_4_out), .in_0({out_10, multiplexer_4_out}), .in_1({EX_ME_out[18:16], EX_ME_out[7:0]}),
    .out(multiplexer_8_out));
  Register #(.Bits(12)) ME_WB (
    .D({EX_ME_out[24], multiplexer_8_out}), .C(CLK_t), .en(1'b1), .Q({ME_WB_q[11], out_11, out_9}));
  RegisterFile #(.AddrBits(3), .Bits(8)) RegFile (
    .Din(out_9), .we(and_3_out), .Rw(multiplexer_5_out), .C(CLK_t), .Ra(ID_R_Src1), .Rb(multiplexer_6_out),
    .Da(out_7), .Db(R_Src_2_Out));
  ALU ALU (
    .A(EX_Data_A), .B(EX_Data_B), .Do_Math(EX_SMTH_Choice), .Res(sddd), .C_F(ALU_c_f[0]), .O_F(ALU_c_f[1]),
    .N_F(ALU_c_f[2]), .Z_F(ALU_c_f[3]));
  Multiplexer #(.Selector_Bits(2)) multiplexer_9 (
    .sel(EX_SMTH_Choice[1:0]), .in_0(EX_Reg_F[0]), .in_1(EX_Reg_F[3]), .in_2(not_3_out), .in_3(1'b1),
    .out(EX_Jump_do));
  not not_4 (not_4_out, EX_ME_out[24]);
  Multiplexer multiplexer_10 (.sel(EX_Jump_en), .in_0(1'b0), .in_1(EX_Jump_do), .out(Go_Branch));
  flag_register flag_register_1 (.CONZ_i(ALU_c_f), .Do_Write(EX_Math_en), .CONZ_o(EX_Reg_F));
  Register WB_IF (.D(ME_WB_q[11]), .C(CLK_t), .en(1'b1), .Q(WB_EN));
  Register #(.Bits(24)) ID_EX (
    .D({rom_1_d, ID_R_Dest, out_7, out_8}), .C(CLK_t), .en(1'b1),
    .Q({EX_Do_SMTH, EX_SMTH_Choice, EX_R_Dest, EX_Data_A, EX_Data_B}));
  Register #(.Bits(25)) EX_ME (.D(multiplexer_12_out), .C(CLK_t), .en(1'b1), .Q(EX_ME_out));
  Multiplexer #(.Selector_Bits(2), .Bits(8)) multiplexer_11 (
    .sel(EX_Do_SMTH), .in_0(sddd), .in_1({8{1'b0}}), .in_2({8{1'b0}}), .in_3(EX_Mem_output),
    .out(multiplexer_11_out));
  Comparator #(.Bits(2)) comparator_1 (.a(EX_Do_SMTH), .b(2'b01), .eq(comparator_1_eq));  // open: gt, lt
  Multiplexer #(.Bits(25)) multiplexer_12 (
    .sel(comparator_1_eq), .in_0({{6{1'b0}}, EX_R_Dest, {8{1'b0}}, multiplexer_11_out}),
    .in_1({1'b1, EX_Do_SMTH, EX_SMTH_Choice, EX_R_Dest, EX_Data_A, EX_Data_B}), .out(multiplexer_12_out));

  assign out_12 = out_9;
  assign out_13 = ddd;
  assign out_14 = ddd;
  assign out_15 = ddd;
  assign out_16 = ddd;
  assign out_17 = ddd;
  assign out_18 = ddd;
  assign out_19 = ddd;

  // Other names for the same wires on the sheet: WB_output[7:0] = out_9; WB_R_Dest[2:0] = out_11; CLK_Lower = in_20;
  //   CLK_Middle = in_21; CLK_Upper = in_22; EX_ALU_output[7:0] = sddd; ME_Data_B[7:0] = EX_ME_out[7:0];
  //   ME_Data_A[7:0] = EX_ME_out[15:8]; ME_R_Dest[2:0] = EX_ME_out[18:16]; ME_SMTH_Choice[2:0] = EX_ME_out[21:19];
  //   ME_Do_SMTH[1:0] = EX_ME_out[23:22]; ME_EN = EX_ME_out[24]; RegF_C = EX_Reg_F[0]; RegF_O = EX_Reg_F[1];
  //   RegF_N = EX_Reg_F[2]; RegF_Z = EX_Reg_F[3]; ID_Data_A[7:0] = out_7; ID_Data_B[7:0] = out_8;
  //   ID_EX[23:0] = {EX_Do_SMTH, EX_SMTH_Choice, EX_R_Dest, EX_Data_A, EX_Data_B}; Line_Branch[7:0] = EX_Data_B;
  //   in_8bit[7:0] = in_8bits; ME_R_DestOut[2:0] = out_10; PC_Out[7:0] = ddd

  // Notes on the sheet:
  //   RegF_WE: default 1
  //   Opcode
  //   0000: LD
  //   0001: MOV
  //   0010: ST
  //   0011: RD
  //   0100: ADD
  //   0101L SUB
  //   0110: MUL
  //   0111: WR
  //   1000: AND
  //   1001: OR
  //   1010: XOR
  //   1011: NOT
  //   1100: BC
  //   1101:BZ
  //   1110: BNZ
  //   1111:B
  //   Pipeline Stages
  //   Instruction Fetch
  //   Execute
  //   Memory
  //   Branch Prediction
  //   Static Guess Not Taken Branch
  //   Do_{Mem}
  //   Might be problem here
  //   Sol: change to 2 bits
  //   and detect for 10
  //   contents of Instruction (hex, n*v repeats v):
  //   44014,44814,45014,45814,46014,54001,54901,55201,7c004,468ff,470ff
  //   IF/ID
  //   PC_{Out}
  //   Instruction Decode
  //   ME/WB
  //   CU
  //   Do_{SMTH}: 4:3
  //   00 Do_{Math}(In:EX -> WB)
  //   01 Do_{GPIO} (In:EX -> ME)
  //   10 Do_{Jump} (IMM only) (In:Somewhere)
  //   11 Do_{Mem} (IMM only) (In:ME)
  //   SMTH_{Choice}: 2:0
  //   Do_{Math}
  //   Do_{Jump}
  //   contents of rom_1 (hex, n*v repeats v):
  //   18,a,19,9,0,1,2,8,4,5,6,7,10,11,12,13
  //   Write Back
  //   ID/EX
  //   EX/ME
endmodule
